// Logisim project Project2Given.circ as structural Verilog: 4 circuits, main circuit main
module main (
);

  wire and_1_out, and_2_out, B0, B1, B2, B3, B4, B5, B6, B7, B8, B9, BL, BU, C0, C1, C2, CLK, L1_l, L1_u,
       not_1_out, or_8_out, P1_b3, R0, R1, R3, R4, Valid;
  wire [2:0] counter_1_q;
  wire [3:0] IB1_c0, P1_b0, register_3_q, register_4_q, register_5_q;

  Button n1 (.out(B1));
  Button n4 (.out(B4));
  Button n7 (.out(B7));
  Button L (.out(BL));
  Button n3 (.out(B3));
  Button n2 (.out(B2));
  Button n6 (.out(B6));
  Button n5 (.out(B5));
  Button n9 (.out(B9));
  Button n8 (.out(B8));
  Button U (.out(BU));
  Button n0 (.out(B0));
  or or_1 (R0, B3, B2, B1);
  or or_2 (R1, B6, B5, B4);
  or or_3 (R3, B9, B8, B7);
  or or_4 (R4, BU, B0, BL);
  or or_5 (C0, B1, B4, B7, BL);
  or or_6 (C1, B2, B5, B8, B0);
  or or_7 (C2, B3, B6, B9, BU);
  Clock clock_1 (.out(CLK));
  nand nand_1 (Valid, IB1_c0[0], IB1_c0[1], IB1_c0[2], IB1_c0[3]);
  // Probe on P1_b0
  Panel P1 (
    .R0(R0), .R1(R1), .R2(R3), .R3(R4), .C0(C0), .C1(C1), .C2(C2), .B0(P1_b0[0]), .B1(P1_b0[1]),
    .B2(P1_b0[2]), .V(P1_b0[3]), .B3(P1_b3));
  LED Press (.in(P1_b3));
  // Probe on IB1_c0
  InputBuffer IB1 (
    .B0(P1_b0[0]), .B1(P1_b0[1]), .B2(P1_b0[2]), .B3(P1_b0[3]), .V(P1_b3), .CLK(not_1_out), .C0(IB1_c0[0]),
    .C1(IB1_c0[1]), .C2(IB1_c0[2]), .C3(IB1_c0[3]));
  not not_1 (not_1_out, CLK);
  Register #(.width(4)) register_1 (.D(register_3_q), .en(Valid), .clk(CLK));  // open: Q, clr
  Lock L1 (.C0(IB1_c0[1]), .C1(IB1_c0[2]), .C2(IB1_c0[3]), .CLK(CLK), .L(L1_l), .U(L1_u));  // open: C3, out_8
  Counter #(.max('h7), .width(3)) counter_1 (
    .count(or_8_out), .Q(counter_1_q), .up(L1_u), .clk(CLK));  // open: load, D, carry, clr
  or or_8 (or_8_out, L1_l, L1_u);
  Register #(.width(4)) register_2 (.D(register_3_q), .en(Valid), .clk(CLK));  // open: Q, clr
  LED Unlocked (.in(and_1_out));
  and and_1 (and_1_out, ~counter_1_q[0], ~counter_1_q[1], ~counter_1_q[2]);  // AND_Gate
  Register #(.width(4)) register_3 (.D(register_4_q), .en(Valid), .clk(CLK), .Q(register_3_q));  // open: clr
  LED Locked (.in(and_2_out));
  and and_2 (and_2_out, ~counter_1_q[0], ~counter_1_q[1], counter_1_q[2]);  // AND_Gate
  Register #(.width(4)) register_4 (.D(register_5_q), .en(Valid), .clk(CLK), .Q(register_4_q));  // open: clr
  Register #(.width(4)) register_5 (.D(IB1_c0), .en(Valid), .clk(CLK), .Q(register_5_q));  // open: clr
endmodule

module Panel (
  input  R0,
  input  R1,
  input  R2,
  input  R3,
  input  C0,
  input  C1,
  input  C2,
  output B0,
  output B1,
  output B2,
  output V,
  output B3
);

  wire or_1_out;
  wire [11:0] R3C1_out;

  and R3C1 (R3C1_out[0], R3, C1);
  and R0C0 (R3C1_out[1], R0, C0);
  and R0C1 (R3C1_out[2], R0, C1);
  and R0C2 (R3C1_out[3], R1, C2);
  and R1C0 (R3C1_out[4], R1, C0);
  and R1C1 (R3C1_out[5], R1, C1);
  and R1C2 (R3C1_out[6], R1, C2);
  and R2C0 (R3C1_out[7], R2, C0);
  and R2C1 (R3C1_out[8], R2, C1);
  and R2C2 (R3C1_out[9], R2, C2);
  and R3C0 (R3C1_out[10], R3, C0);
  and R3C2 (R3C1_out[11], R3, C2);
  Priority_Encoder #(.select(4)) priority_encoder_1 (
    .in0(R3C1_out[0]), .in1(R3C1_out[1]), .in2(R3C1_out[2]), .in3(R3C1_out[3]), .in4(R3C1_out[4]),
    .in5(R3C1_out[5]), .in6(R3C1_out[6]), .in7(R3C1_out[7]), .in8(R3C1_out[8]), .in9(R3C1_out[9]),
    .in10(R3C1_out[10]), .in11(R3C1_out[11]), .out({B3, B2, B1, B0}), .en_in(or_1_out));  // open: in12, in13, in14, in15, gs, en_out
  or or_1 (or_1_out, R3C1_out[0], R3C1_out[1], R3C1_out[2], R3C1_out[3], R3C1_out[4], R3C1_out[5], R3C1_out[6], R3C1_out[7], R3C1_out[8], R3C1_out[9], R3C1_out[10], R3C1_out[11], 1'b0);
  ExactlyOne xor_1 (
    .out(V), .in0(R3C1_out[0]), .in1(R3C1_out[1]), .in2(R3C1_out[2]), .in3(R3C1_out[3]), .in4(R3C1_out[4]),
    .in5(R3C1_out[5]), .in6(R3C1_out[6]), .in7(R3C1_out[7]), .in8(R3C1_out[8]), .in9(R3C1_out[9]),
    .in10(R3C1_out[10]), .in11(R3C1_out[11]));
endmodule

module InputBuffer (
  input  B0,
  input  B1,
  input  B2,
  input  B3,
  input  V,
  input  CLK,
  output C0,
  output C1,
  output C2,
  output C3
);

  wire d_ff_2_q, IdleState, not_1_out, OpenState, xor_1_out;

  D_Flip_Flop d_ff_1 (.D(V), .clk(CLK), .Q(OpenState));  // open: Qn, preset, reset
  D_Flip_Flop d_ff_2 (.D(OpenState), .clk(CLK), .Q(d_ff_2_q));  // open: Qn, preset, reset
  Multiplexer #(.width(4)) multiplexer_1 (
    .in0(4'b1111), .in1({B3, B2, B1, B0}), .out({C3, C2, C1, C0}), .sel(xor_1_out));
  xor xor_1 (xor_1_out, OpenState, IdleState);
  not not_1 (not_1_out, V);
  xor xor_2 (IdleState, d_ff_2_q, not_1_out);

  // Notes on the sheet:
  //   Still need to handle during cycle 1, C0, C1 C2 C3 output should not change  when other buttons are pressed
endmodule

module Lock (
  input  C0,
  input  C1,
  input  C2,
  input  C3,
  input  CLK,
  output L,
  output U,
  output out_8
);

  wire and_1_out, and_2_out, and_3_out, and_4_out, and_5_out, and_11_out, and_12_out, and_14_out, and_15_out,
       ButtonPress, controlled_buffer_1_out, d_ff_2_q, d_ff_4_q, d_ff_5_q, d_ff_6_q, d_ff_7_q, d_ff_9_q,
       Locked, Lpressed, LUlocked, LUlocking, LUuncloked, LUunlocking, not_1_out, not_2_out, ToLockingState,
       ToLockingState2, Value, xor_1_out, xor_2_out;

  not not_1 (not_1_out, C0);
  and and_1 (and_1_out, not_1_out, 1'b1);
  and and_2 (and_2_out, C1, 1'b1);
  not not_2 (not_2_out, C2);
  and and_3 (and_3_out, not_2_out, 1'b1);
  and and_4 (and_4_out, C3, 1'b1);
  xor xor_1 (xor_1_out, Locked, Value);
  xor xor_2 (xor_2_out, ToLockingState, ToLockingState2);
  Multiplexer multiplexer_1 (.in0(1'b0), .in1(1'b1), .sel(xor_1_out));  // open: out
  or or_1 (ButtonPress, C0, C1, C2, C3);
  and and_5 (and_5_out, and_1_out, and_2_out, and_3_out, and_4_out);
  // AND_Gate and_6 has open pins: in0=LUuncloked, out=open
  // AND_Gate and_7 has open pins: in0=LUlocking, in1=1'b1, out=open
  // AND_Gate and_8 has open pins: in0=LUlocked, out=open
  // AND_Gate and_9 has open pins: in0=LUunlocking, out=open
  D_Flip_Flop d_ff_1 (.D(and_5_out), .clk(controlled_buffer_1_out), .Q(Lpressed));  // open: Qn, preset, reset
  assign controlled_buffer_1_out = and_5_out ? CLK : 1'bz;  // Controlled_Buffer controlled_buffer_1
  or or_2 (Value, xor_2_out, d_ff_2_q);
  D_Flip_Flop d_ff_2 (.D(xor_2_out), .clk(CLK), .Q(d_ff_2_q));  // open: Qn, preset, reset
  and and_10 (LUlocking, xor_1_out, 1'b1);
  and and_11 (and_11_out, Lpressed, 1'b1);
  // OR_Gate or_3 is placed but not wired
  D_Flip_Flop d_ff_3 (.D(Lpressed), .clk(controlled_buffer_1_out), .Q(out_8));  // open: Qn, preset, reset
  D_Flip_Flop d_ff_4 (.D(and_11_out), .clk(CLK), .Q(d_ff_4_q));  // open: Qn, preset, reset
  D_Flip_Flop d_ff_5 (.D(d_ff_2_q), .clk(CLK), .Q(d_ff_5_q));  // open: Qn, preset, reset
  and and_12 (and_12_out, ButtonPress, d_ff_4_q);
  D_Flip_Flop d_ff_6 (.D(and_12_out), .clk(CLK), .Q(d_ff_6_q));  // open: Qn, preset, reset
  D_Flip_Flop d_ff_7 (.D(d_ff_5_q), .clk(CLK), .Q(d_ff_7_q));  // open: Qn, preset, reset
  and and_13 (ToLockingState, Lpressed, out_8);
  and and_14 (and_14_out, ButtonPress, d_ff_6_q);
  D_Flip_Flop d_ff_8 (.D(d_ff_7_q), .clk(CLK), .Q(Locked));  // open: Qn, preset, reset
  D_Flip_Flop d_ff_9 (.D(and_14_out), .clk(CLK), .Q(d_ff_9_q));  // open: Qn, preset, reset
  D_Flip_Flop d_ff_10 (.D(Locked), .clk(CLK));  // open: Q, Qn, preset, reset
  and and_15 (and_15_out, ButtonPress, d_ff_9_q);
  D_Flip_Flop d_ff_11 (.D(and_15_out), .clk(CLK), .Q(ToLockingState2));  // open: Qn, preset, reset

  // Other names for the same wires on the sheet: Lpressed2 = out_8

  // Notes on the sheet:
  //   use for detecting digit press
  //   If L is pressed, then followed by 3 consecutive  (valid) digit
  //   LU value in locking stage( hold 4 cycle)
  //   Note: Part 2 already handled when valid press only last for one cycle.
  //   Start counting 3 digit consec on this D-flip-flop
endmodule
