// Logisim project Project2GivenTest.circ as structural Verilog: 4 circuits, main circuit main
module main (
);

  wire and_1_out, and_2_out, B0, B1, B2, B3, B4, B5, B6, B7, B8, B9, BL, BU, C0, C1, C2, CLK, L1_p8, L1_p9,
       not_1_out, or_8_out, P1_b3, R0, R1, R3, R4, Valid;
  wire [2:0] counter_1_q;
  wire [3:0] IB1_c0, L1_p7, P1_b0, register_4_q, register_5_q;

  Button n1 (.out(B1));
  Button n4 (.out(B4));
  Button n7 (.out(B7));
  Button L (.out(BL));
  Button n3 (.out(B3));
  Button n2 (.out(B2));
  Button n6 (.out(B6));
  Button n5 (.out(B5));
  Button n9 (.out(B9));
  Button n8 (.out(B8));
  Button U (.out(BU));
  Button n0 (.out(B0));
  or or_1 (R0, B3, B2, B1);
  or or_2 (R1, B6, B5, B4);
  or or_3 (R3, B9, B8, B7);
  or or_4 (R4, BU, B0, BL);
  or or_5 (C0, B1, B4, B7, BL);
  or or_6 (C1, B2, B5, B8, B0);
  or or_7 (C2, B3, B6, B9, BU);
  Clock clock_1 (.out(CLK));
  nand nand_1 (Valid, IB1_c0[0], IB1_c0[1], IB1_c0[2], IB1_c0[3]);
  // Probe on P1_b0
  Panel P1 (
    .R0(R0), .R1(R1), .R2(R3), .R3(R4), .C0(C0), .C1(C1), .C2(C2), .B0(P1_b0[0]), .B1(P1_b0[1]),
    .B2(P1_b0[2]), .V(P1_b0[3]), .B3(P1_b3));
  LED Press (.in(P1_b3));
  // Probe on IB1_c0
  InputBuffer IB1 (
    .B0(P1_b0[0]), .B1(P1_b0[1]), .B2(P1_b0[2]), .B3(P1_b0[3]), .V(P1_b3), .CLK(not_1_out), .C0(IB1_c0[0]),
    .C1(IB1_c0[1]), .C2(IB1_c0[2]), .C3(IB1_c0[3]));
  not not_1 (not_1_out, CLK);
  Register #(.width(4)) register_1 (.D(L1_p7), .en(Valid), .clk(CLK));  // open: Q, clr
  // Lock L1: pin names not known; wires that end beside it: IB1_c0[0], IB1_c0[1], IB1_c0[2], IB1_c0[3], IB1_c0, CLK, L1_p7, L1_p8, L1_p9
  Counter #(.max('h7), .width(3)) counter_1 (
    .count(or_8_out), .Q(counter_1_q), .up(L1_p9), .clk(CLK));  // open: load, D, carry, clr
  or or_8 (or_8_out, L1_p8, L1_p9);
  Register #(.width(4)) register_2 (.D(L1_p7), .en(Valid), .clk(CLK));  // open: Q, clr
  LED Unlocked (.in(and_1_out));
  and and_1 (and_1_out, ~counter_1_q[0], ~counter_1_q[1], ~counter_1_q[2]);  // AND_Gate
  Register #(.width(4)) register_3 (.D(register_4_q), .en(Valid), .clk(CLK), .Q(L1_p7));  // open: clr
  LED Locked (.in(and_2_out));
  and and_2 (and_2_out, ~counter_1_q[0], ~counter_1_q[1], counter_1_q[2]);  // AND_Gate
  Register #(.width(4)) register_4 (.D(register_5_q), .en(Valid), .clk(CLK), .Q(register_4_q));  // open: clr
  Register #(.width(4)) register_5 (.D(IB1_c0), .en(Valid), .clk(CLK), .Q(register_5_q));  // open: clr
endmodule

module Panel (
  input  R0,
  input  R1,
  input  R2,
  input  R3,
  input  C0,
  input  C1,
  input  C2,
  output B0,
  output B1,
  output B2,
  output V,
  output B3
);

  wire or_1_out;
  wire [11:0] R3C1_out;

  and R3C1 (R3C1_out[0], R3, C1);
  and R0C0 (R3C1_out[1], R0, C0);
  and R0C1 (R3C1_out[2], R0, C1);
  and R0C2 (R3C1_out[3], R1, C2);
  and R1C0 (R3C1_out[4], R1, C0);
  and R1C1 (R3C1_out[5], R1, C1);
  and R1C2 (R3C1_out[6], R1, C2);
  and R2C0 (R3C1_out[7], R2, C0);
  and R2C1 (R3C1_out[8], R2, C1);
  and R2C2 (R3C1_out[9], R2, C2);
  and R3C0 (R3C1_out[10], R3, C0);
  and R3C2 (R3C1_out[11], R3, C2);
  Priority_Encoder #(.select(4)) priority_encoder_1 (
    .in0(R3C1_out[0]), .in1(R3C1_out[1]), .in2(R3C1_out[2]), .in3(R3C1_out[3]), .in4(R3C1_out[4]),
    .in5(R3C1_out[5]), .in6(R3C1_out[6]), .in7(R3C1_out[7]), .in8(R3C1_out[8]), .in9(R3C1_out[9]),
    .in10(R3C1_out[10]), .in11(R3C1_out[11]), .out({B3, B2, B1, B0}), .en_in(or_1_out));  // open: in12, in13, in14, in15, gs, en_out
  or or_1 (or_1_out, R3C1_out[0], R3C1_out[1], R3C1_out[2], R3C1_out[3], R3C1_out[4], R3C1_out[5], R3C1_out[6], R3C1_out[7], R3C1_out[8], R3C1_out[9], R3C1_out[10], R3C1_out[11], 1'b0);
  ExactlyOne xor_1 (
    .out(V), .in0(R3C1_out[0]), .in1(R3C1_out[1]), .in2(R3C1_out[2]), .in3(R3C1_out[3]), .in4(R3C1_out[4]),
    .in5(R3C1_out[5]), .in6(R3C1_out[6]), .in7(R3C1_out[7]), .in8(R3C1_out[8]), .in9(R3C1_out[9]),
    .in10(R3C1_out[10]), .in11(R3C1_out[11]));
endmodule

module InputBuffer (
  input  B0,
  input  B1,
  input  B2,
  input  B3,
  input  V,
  input  CLK,
  output C0,
  output C1,
  output C2,
  output C3
);

  wire d_ff_2_q, IdleState, not_1_out, OpenState, xor_1_out;

  D_Flip_Flop d_ff_1 (.D(V), .clk(CLK), .Q(OpenState));  // open: Qn, preset, reset
  D_Flip_Flop d_ff_2 (.D(OpenState), .clk(CLK), .Q(d_ff_2_q));  // open: Qn, preset, reset
  Multiplexer #(.width(4)) multiplexer_1 (
    .in0(4'b1111), .in1({B3, B2, B1, B0}), .out({C3, C2, C1, C0}), .sel(xor_1_out));
  xor xor_1 (xor_1_out, OpenState, IdleState);
  not not_1 (not_1_out, V);
  xor xor_2 (IdleState, d_ff_2_q, not_1_out);

  // Notes on the sheet:
  //   Still need to handle during cycle 1, C0, C1 C2 C3 output should not change  when other buttons are pressed
endmodule

module Lock (
  input  C0,
  input  C1,
  input  C2,
  input  C3,
  input  CLK,
  input  in_6,
  input  [3:0] in_7,
  input  in_8,
  input  in_9,
  input  in_10,
  input  [1:0] in_11,
  input  in_12,
  input  [1:0] in_13,
  input  in_14,
  input  [1:0] in_15,
  input  in_16,
  input  in_17,
  output L,
  output U,
  output out_20,
  output out_21,
  output [3:0] out_22,
  output [1:0] out_23,
  output [1:0] out_24
);

  wire and_1_out, and_10_out, and_11_out, and_12_out, and_13_out, and_15_out, and_16_out, ButtonPress, clear,
       clock_1_out, clock_2_out, controlled_buffer_1_out, controlled_buffer_2_out, d_ff_4_q, d_ff_5_q,
       d_ff_6_q, d_ff_8_q, d_ff_9_q, d_ff_10_q, d_ff_11_q, Lcode, Locked, Lpressed, LUlocked, LUlocking,
       LUuncloked, LUunlocking, not_1_out, not_2_out, not_3_out, not_4_out, not_5_out, not_6_out, not_7_out,
       notL, ToLockingState, ToLockingState2, Ucode, Value, xor_3_out, xor_5_out;
  wire [1:0] counter_2_q;

  Clock clock_1 (.out(clock_1_out));
  D_Flip_Flop d_ff_1 (.D(in_6), .clk(clock_1_out), .Q(out_20));  // open: Qn, preset, reset
  and and_1 (and_1_out, Lpressed, 1'b1);
  Counter #(.max('h3), .width(2)) counter_1 (
    .D(in_15), .Q(out_24), .clk(in_16), .clr(in_17));  // open: load, count, carry, up
  Register #(.width(4)) register_1 (.D(in_7), .en(in_8), .clk(in_9), .Q(out_22));  // open: clr
  not not_1 (not_1_out, C2);
  not not_2 (not_2_out, C0);
  not not_3 (not_3_out, C2);
  Counter #(.max('h3), .width(2)) counter_2 (
    .load(in_12), .D(in_13), .Q(counter_2_q), .clk(and_1_out));  // open: count, carry, up, clr
  and and_2 (Ucode, C0, C1, not_1_out, C3);
  and and_3 (Lcode, not_2_out, C1, not_3_out, C3);
  Counter #(.max('h3), .width(2)) counter_3 (
    .load(in_10), .D(in_11), .Q(out_23), .clk(and_1_out), .clr(clear));  // open: count, carry, up
  not not_4 (not_4_out, Lpressed);
  // XOR_Gate xor_1 has open pins: in0=Ucode, in1=out_21, out=open
  // XOR_Gate xor_2 is placed but not wired
  // AND_Gate and_4 has open pins: in0=LUuncloked, out=open
  // AND_Gate and_5 has open pins: in0=LUlocking, in1=1'b1, out=open
  // AND_Gate and_6 has open pins: in0=LUlocked, out=open
  // AND_Gate and_7 has open pins: in0=LUunlocking, out=open
  not not_5 (not_5_out, counter_2_q[1]);
  and and_8 (clear, not_4_out, notL);
  D_Flip_Flop d_ff_2 (.D(Lcode), .clk(CLK), .Q(Lpressed));  // open: Qn, preset, reset
  and and_9 (notL, out_23[0], not_6_out);
  not not_6 (not_6_out, out_23[1]);
  not not_7 (not_7_out, out_23[0]);
  and and_10 (and_10_out, not_7_out, out_23[1]);
  and and_11 (and_11_out, counter_2_q[0], not_5_out);
  or or_1 (ButtonPress, C0, C1, C2, C3);
  and and_12 (and_12_out, Lpressed, 1'b1);
  // OR_Gate or_2 is placed but not wired
  Clock clock_2 (.out(clock_2_out));
  D_Flip_Flop d_ff_3 (
    .D(controlled_buffer_1_out), .clk(controlled_buffer_2_out), .Q(out_21));  // open: Qn, preset, reset
  assign controlled_buffer_1_out = Lcode ? Lpressed : 1'bz;  // Controlled_Buffer controlled_buffer_1
  assign controlled_buffer_2_out = controlled_buffer_1_out ? CLK : 1'bz;  // Controlled_Buffer controlled_buffer_2
  D_Flip_Flop d_ff_4 (.D(and_12_out), .clk(CLK), .Q(d_ff_4_q));  // open: Qn, preset, reset
  D_Flip_Flop d_ff_5 (.D(and_11_out), .clk(clock_2_out), .Q(d_ff_5_q));  // open: Qn, preset, reset
  and and_13 (and_13_out, ButtonPress, d_ff_4_q);
  // AND_Gate validpress has open pins: in0=ButtonPress, in1=and_11_out, out=open
  D_Flip_Flop d_ff_6 (.D(and_13_out), .clk(CLK), .Q(d_ff_6_q));  // open: Qn, preset, reset
  and and_14 (ToLockingState, Lpressed, out_21);
  and and_15 (and_15_out, ButtonPress, d_ff_6_q);
  xor xor_3 (xor_3_out, ToLockingState, ToLockingState2);
  D_Flip_Flop d_ff_7 (.D(d_ff_5_q));  // open: clk, Q, Qn, preset, reset
  D_Flip_Flop d_ff_8 (.D(and_15_out), .clk(CLK), .Q(d_ff_8_q));  // open: Qn, preset, reset
  or or_3 (Value, xor_3_out, d_ff_9_q);
  D_Flip_Flop d_ff_9 (.D(xor_3_out), .clk(CLK), .Q(d_ff_9_q));  // open: Qn, preset, reset
  and and_16 (and_16_out, ButtonPress, d_ff_8_q);
  D_Flip_Flop d_ff_10 (.D(d_ff_9_q), .clk(CLK), .Q(d_ff_10_q));  // open: Qn, preset, reset
  xor xor_4 (ToLockingState2, and_16_out, Ucode);
  D_Flip_Flop d_ff_11 (.D(d_ff_10_q), .clk(CLK), .Q(d_ff_11_q));  // open: Qn, preset, reset
  xor xor_5 (xor_5_out, Locked, Value);
  D_Flip_Flop d_ff_12 (.D(d_ff_11_q), .clk(CLK), .Q(Locked));  // open: Qn, preset, reset
  Multiplexer multiplexer_1 (.in0(1'b0), .in1(1'b1), .sel(xor_5_out));  // open: out
  D_Flip_Flop d_ff_13 (.D(Locked), .clk(CLK));  // open: Q, Qn, preset, reset
  and and_17 (LUlocking, xor_5_out, 1'b1);

  // Other names for the same wires on the sheet: Lpressed2 = out_21

  // Notes on the sheet:
  //   Clear the counter(back to inital unlocked state) if L is not pressed again after L
  //   If L is pressed, then followed by 3 consecutive  (valid) digit
  //   Use to clear the counter if L is not pressed again. Note: notL is at "01"
  //   use for detecting digit press
  //   Note: Part 2 should already handled when valid press only last for one cycle.
  //   Start counting 3 digit consec on this D-flip-flop
  //   LU value in locking stage( hold 4 cycle)
endmodule
